# Fritzing sketch Wifi_Radio_Wiring (saved by Fritzing 0.9.3b)
breadboards: 1

parts:
  Raspberry_Pi1 = Raspberry Pi B rev2
  Bauteil1 = Arduino Pro Mini v13
  Bauteil2 = Arduino Pro Mini v13
  U1 = LCD-16X2 [package=lcd-16x2]
  Bauteil3 = Logic Level Converter
  ENC_KURZ = Rotary Encoder with Knob
  ENC_LANG = Rotary Encoder with Knob
  R1 = Resistor [tolerance=±5% resistance=680 package=THT]

nets:
  5V: Raspberry_Pi1.5V, U1.VDD, Bauteil3.HV, R1.Pin_1
  GND: Raspberry_Pi1.GND, Bauteil2.GND, U1.VSS, U1.VO, U1.R_W, U1.K, Bauteil3.GND
  N1: Raspberry_Pi1.GPIO_23, U1.DB6
  N2: Raspberry_Pi1.GPIO_17, Bauteil3.RX_HV
  N3: Raspberry_Pi1.GPIO_18, U1.DB7
  N4: Raspberry_Pi1.GPIO_27, Bauteil3.RX2_HV
  N5: Raspberry_Pi1.GPIO_22, Bauteil3.TX2_HV
  N6: Raspberry_Pi1.GPIO_4, Bauteil3.TX_HV
  N7: Raspberry_Pi1.GPIO_24, U1.DB5
  N8: Raspberry_Pi1.GPIO_25, U1.DB4
  N9: Raspberry_Pi1.GPIO_8, U1.E
  N10: Raspberry_Pi1.GPIO_7, U1.RS
  N11: Bauteil1.A3, ENC_KURZ.no_name_yet#3
  N12: Bauteil1.A2, ENC_KURZ.no_name_yet#1, ENC_KURZ.no_name_yet#2
  N13: Bauteil1.A1, Bauteil3.RX_LV
  N14: Bauteil1.A0, Bauteil1.D13/SCK, Bauteil3.TX_LV
  N15: Bauteil2.VCC, Bauteil3.LV
  N16: Bauteil2.A3, ENC_LANG.no_name_yet#3
  N17: Bauteil2.A2, ENC_LANG.no_name_yet#1
  N18: Bauteil2.A1, Bauteil3.RX2_LV
  N19: Bauteil2.A0, Bauteil3.TX2_LV
  N20: U1.A, R1.Pin_0

custom parts:
  Rotary Encoder with Knob: Rotary Encoder with 1/4" Shaft and Knob
